# Fritzing sketch Circuit_Dustbin (saved by Fritzing 0.9.3b)
breadboards: 1

parts:
  HC-SR04_Sensor_1 = HC-SR04 Ultrasonic Distance Sensor
  Part1 = Arduino Uno (Rev3) - ICSP
  Part2 = Soil Moisture Sensor
  DHT1 = Humidity and Temperature Sensor DHT11
  M1 = Dagu DGServo 9g (Pan and tilt) [part_number=RS001B]
  LED1 = LED - 5mm [color="Red (633nm)" package="5 mm [THT]"]
  LED2 = smd LED [color="Red (633nm)" package="0805 [SMD]"]

nets:
  VCC: HC-SR04_Sensor_1.VCC, Part1.5V, Part2.VCC, M1.vcc
  N1: HC-SR04_Sensor_1.TRIG, Part1.D6_PWM
  N2: HC-SR04_Sensor_1.ECHO, Part1.D7
  GND: HC-SR04_Sensor_1.GND, Part1.GND, DHT1.GND_2, M1.gnd, LED1.cathode, LED2.cathode
  N3: Part1.A0, DHT1.Data-signal
  N4: Part1.A1, Part2.SIG
  N5: Part1.A2, M1.pulse
  N6: Part1.D2, LED1.anode
  N7: Part1.D3_PWM, LED2.anode

custom parts:
  Humidity and Temperature Sensor DHT11: Digital relative humidity & temperature sensor DHT11
